// Logisim project calculatrice.circ as structural Verilog: 11 circuits, main circuit 7-segments
module _7_segments (
  input  D,
  input  C,
  input  B,
  input  A,
  output a_2,
  output f,
  output g,
  output e,
  output d_2,
  output b_2,
  output c_2
);

  wire and_1_out, and_2_out, and_3_out, and_4_out, and_5_out, and_6_out, and_7_out, and_8_out, and_9_out,
       and_10_out, not_1_out, not_2_out, not_3_out, not_4_out, or_1_out, or_3_out, or_4_out, or_6_out,
       or_7_out, or_8_out, or_10_out, or_12_out, or_14_out, or_15_out, or_17_out, or_18_out;

  not not_1 (not_1_out, D);
  not not_2 (not_2_out, B);
  not not_3 (not_3_out, C);
  not not_4 (not_4_out, A);
  and and_1 (and_1_out, not_4_out, not_2_out, not_3_out, not_1_out);
  and and_2 (and_2_out, A, not_2_out, not_3_out, not_1_out);
  and and_3 (and_3_out, not_4_out, B, not_3_out, not_1_out);
  and and_4 (and_4_out, A, B, not_3_out, not_1_out);
  and and_5 (and_5_out, not_4_out, not_2_out, C, not_1_out);
  and and_6 (and_6_out, A, not_2_out, C, not_1_out);
  and and_7 (and_7_out, not_4_out, B, C, not_1_out);
  and and_8 (and_8_out, A, B, C, not_1_out);
  and and_9 (and_9_out, not_4_out, not_2_out, not_3_out, D);
  and and_10 (and_10_out, A, not_2_out, not_3_out, D);
  or or_1 (or_1_out, and_1_out, and_3_out, and_4_out, and_6_out, and_7_out);
  or or_2 (a_2, or_1_out, or_3_out);
  or or_3 (or_3_out, and_8_out, and_9_out, and_10_out);
  or or_4 (or_4_out, and_3_out, and_4_out, and_5_out, and_6_out, and_7_out);
  or or_5 (g, or_4_out, or_6_out);
  or or_6 (or_6_out, and_9_out, and_10_out);
  or or_7 (or_7_out, and_1_out, and_3_out, and_4_out, and_6_out);
  or or_8 (or_8_out, and_7_out, and_9_out, and_10_out);
  or or_9 (d_2, or_7_out, or_8_out);
  or or_10 (or_10_out, and_6_out, and_5_out, and_1_out);
  or or_11 (f, or_10_out, or_12_out);
  or or_12 (or_12_out, and_7_out, and_9_out, and_10_out);
  or or_13 (e, and_1_out, and_3_out, and_7_out, and_9_out);
  or or_14 (or_14_out, and_1_out, and_2_out, and_3_out, and_4_out, and_5_out);
  or or_15 (or_15_out, and_8_out, and_9_out, and_10_out);
  or or_16 (b_2, or_14_out, or_15_out);
  or or_17 (or_17_out, and_1_out, and_2_out, and_4_out, and_5_out, and_6_out);
  or or_18 (or_18_out, and_7_out, and_8_out, and_9_out, and_10_out);
  or or_19 (c_2, or_17_out, or_18_out);
endmodule

module test_7_segments (
  input  in_1,
  input  in_2,
  input  in_3,
  input  in_4
);

  wire n7_segments_1_a_2, n7_segments_1_b_2, n7_segments_1_c_2, n7_segments_1_d_2, n7_segments_1_e,
       n7_segments_1_f, n7_segments_1_g;

  _7_segments u_7_segments_1 (
    .D(in_1), .C(in_2), .B(in_3), .A(in_4), .a_2(n7_segments_1_a_2), .f(n7_segments_1_f),
    .g(n7_segments_1_g), .e(n7_segments_1_e), .d_2(n7_segments_1_d_2), .b_2(n7_segments_1_b_2),
    .c_2(n7_segments_1_c_2));
  _7_Segment_Display u_7_segment_display_1 (
    .g(n7_segments_1_g), .f(n7_segments_1_f), .a(n7_segments_1_a_2), .b(n7_segments_1_b_2),
    .e(n7_segments_1_e), .d(n7_segments_1_d_2), .c(n7_segments_1_c_2));  // open: dp
endmodule

module bit___bit_et_retenue (
  input  bit_1,
  input  bit_2,
  input  bit_3,
  output bit_de_sortie,
  output retenue
);

  wire and_1_out, and_2_out, and_3_out, and_4_out, and_5_out, and_6_out, and_7_out, and_8_out, and_9_out,
       not_1_out, not_2_out, not_3_out, not_4_out, not_5_out, or_1_out, or_2_out, or_3_out, or_4_out;

  not not_1 (not_1_out, bit_1);
  not not_2 (not_2_out, bit_3);
  not not_3 (not_3_out, bit_2);
  and and_1 (and_1_out, bit_1, not_3_out, not_2_out);
  and and_2 (and_2_out, not_1_out, bit_2, not_2_out);
  and and_3 (and_3_out, not_1_out, not_3_out, bit_3);
  and and_4 (and_4_out, bit_1, bit_2, not_2_out);
  and and_5 (and_5_out, not_1_out, bit_2, bit_3);
  and and_6 (and_6_out, bit_1, not_3_out, bit_3);
  and and_7 (and_7_out, not_1_out, not_3_out, not_2_out);
  not not_4 (not_4_out, and_7_out);
  or or_1 (or_1_out, and_1_out, and_2_out, and_3_out);
  or or_2 (or_2_out, and_4_out, and_5_out, and_6_out);
  not not_5 (not_5_out, or_2_out);
  or or_3 (or_3_out, not_4_out, not_5_out);
  and and_8 (and_8_out, bit_1, bit_2, bit_3);
  and and_9 (and_9_out, or_3_out, or_1_out);
  not not_6 (retenue, or_4_out);
  or or_4 (or_4_out, and_7_out, or_1_out);
  or or_5 (bit_de_sortie, and_9_out, and_8_out);
endmodule

module conversion_affichage_4_bits_maximum_5_bits (
  input  e4,
  input  e3,
  input  e2,
  input  e1,
  input  e0,
  output s7,
  output s6,
  output s5,
  output s4,
  output s3,
  output s2,
  output s1,
  output s0
);

  wire [7:0] divider_1_out, multiplier_1_out;

  Multiplier multiplier_1 (.a(divider_1_out), .b(8'h6), .out(multiplier_1_out));  // open: cin, cout
  Adder adder_1 (
    .a(multiplier_1_out), .b({3'b000, e4, e3, e2, e1, e0}), .out({s7, s6, s5, s4, s3, s2, s1, s0}));  // open: cin, cout
  Divider divider_1 (.a({3'b000, e4, e3, e2, e1, e0}), .b(8'ha), .out(divider_1_out));  // open: upper, rem
endmodule

module \démo__4_bits___4_bits  (
  input  in_1,
  input  in_2,
  input  in_3,
  input  in_4,
  input  in_5,
  input  in_6,
  input  in_7,
  input  in_8,
  output out_9,
  output out_10,
  output out_11,
  output out_12,
  output out_13
);

  wire bit_bit_et_retenue_1_retenue, bit_bit_et_retenue_2_retenue, bit_bit_et_retenue_3_retenue,
       conversion_affichage_4_bits_maximum_5_bits_1_s0, conversion_affichage_4_bits_maximum_5_bits_1_s1,
       conversion_affichage_4_bits_maximum_5_bits_1_s2, conversion_affichage_4_bits_maximum_5_bits_1_s3,
       conversion_affichage_4_bits_maximum_5_bits_1_s4, conversion_affichage_4_bits_maximum_5_bits_1_s5,
       conversion_affichage_4_bits_maximum_5_bits_1_s6, conversion_affichage_4_bits_maximum_5_bits_1_s7,
       conversion_affichage_4_bits_maximum_5_bits_2_s0, conversion_affichage_4_bits_maximum_5_bits_2_s1,
       conversion_affichage_4_bits_maximum_5_bits_2_s2, conversion_affichage_4_bits_maximum_5_bits_2_s3,
       conversion_affichage_4_bits_maximum_5_bits_2_s4, conversion_affichage_4_bits_maximum_5_bits_2_s5,
       conversion_affichage_4_bits_maximum_5_bits_2_s6, conversion_affichage_4_bits_maximum_5_bits_2_s7,
       conversion_affichage_4_bits_maximum_5_bits_3_s0, conversion_affichage_4_bits_maximum_5_bits_3_s1,
       conversion_affichage_4_bits_maximum_5_bits_3_s2, conversion_affichage_4_bits_maximum_5_bits_3_s3,
       conversion_affichage_4_bits_maximum_5_bits_3_s4, conversion_affichage_4_bits_maximum_5_bits_3_s5,
       conversion_affichage_4_bits_maximum_5_bits_3_s6, conversion_affichage_4_bits_maximum_5_bits_3_s7,
       n7_segments_1_a_2, n7_segments_1_b_2, n7_segments_1_c_2, n7_segments_1_d_2, n7_segments_1_e,
       n7_segments_1_f, n7_segments_1_g, n7_segments_2_a_2, n7_segments_2_b_2, n7_segments_2_c_2,
       n7_segments_2_d_2, n7_segments_2_e, n7_segments_2_f, n7_segments_2_g, n7_segments_3_a_2,
       n7_segments_3_b_2, n7_segments_3_c_2, n7_segments_3_d_2, n7_segments_3_e, n7_segments_3_f,
       n7_segments_3_g, n7_segments_4_a_2, n7_segments_4_b_2, n7_segments_4_c_2, n7_segments_4_d_2,
       n7_segments_4_e, n7_segments_4_f, n7_segments_4_g, n7_segments_5_a_2, n7_segments_5_b_2,
       n7_segments_5_c_2, n7_segments_5_d_2, n7_segments_5_e, n7_segments_5_f, n7_segments_5_g,
       n7_segments_6_a_2, n7_segments_6_b_2, n7_segments_6_c_2, n7_segments_6_d_2, n7_segments_6_e,
       n7_segments_6_f, n7_segments_6_g;

  bit___bit_et_retenue bit_bit_et_retenue_1 (
    .bit_1(in_4), .bit_2(in_8), .bit_3(1'b0), .bit_de_sortie(out_13), .retenue(bit_bit_et_retenue_1_retenue));
  bit___bit_et_retenue bit_bit_et_retenue_2 (
    .bit_1(in_3), .bit_2(in_7), .bit_3(bit_bit_et_retenue_1_retenue), .bit_de_sortie(out_12),
    .retenue(bit_bit_et_retenue_2_retenue));
  bit___bit_et_retenue bit_bit_et_retenue_3 (
    .bit_1(in_2), .bit_2(in_6), .bit_3(bit_bit_et_retenue_2_retenue), .bit_de_sortie(out_11),
    .retenue(bit_bit_et_retenue_3_retenue));
  bit___bit_et_retenue bit_bit_et_retenue_4 (
    .bit_1(in_1), .bit_2(in_5), .bit_3(bit_bit_et_retenue_3_retenue), .bit_de_sortie(out_10), .retenue(out_9));
  conversion_affichage_4_bits_maximum_5_bits conversion_affichage_4_bits_maximum_5_bits_1 (
    .e4(1'b0), .e3(in_1), .e2(in_2), .e1(in_3), .e0(in_4),
    .s7(conversion_affichage_4_bits_maximum_5_bits_1_s7),
    .s6(conversion_affichage_4_bits_maximum_5_bits_1_s6),
    .s5(conversion_affichage_4_bits_maximum_5_bits_1_s5),
    .s4(conversion_affichage_4_bits_maximum_5_bits_1_s4),
    .s3(conversion_affichage_4_bits_maximum_5_bits_1_s3),
    .s2(conversion_affichage_4_bits_maximum_5_bits_1_s2),
    .s1(conversion_affichage_4_bits_maximum_5_bits_1_s1), .s0(conversion_affichage_4_bits_maximum_5_bits_1_s0));
  conversion_affichage_4_bits_maximum_5_bits conversion_affichage_4_bits_maximum_5_bits_2 (
    .e4(1'b0), .e3(in_5), .e2(in_6), .e1(in_7), .e0(in_8),
    .s7(conversion_affichage_4_bits_maximum_5_bits_2_s7),
    .s6(conversion_affichage_4_bits_maximum_5_bits_2_s6),
    .s5(conversion_affichage_4_bits_maximum_5_bits_2_s5),
    .s4(conversion_affichage_4_bits_maximum_5_bits_2_s4),
    .s3(conversion_affichage_4_bits_maximum_5_bits_2_s3),
    .s2(conversion_affichage_4_bits_maximum_5_bits_2_s2),
    .s1(conversion_affichage_4_bits_maximum_5_bits_2_s1), .s0(conversion_affichage_4_bits_maximum_5_bits_2_s0));
  conversion_affichage_4_bits_maximum_5_bits conversion_affichage_4_bits_maximum_5_bits_3 (
    .e4(out_9), .e3(out_10), .e2(out_11), .e1(out_12), .e0(out_13),
    .s7(conversion_affichage_4_bits_maximum_5_bits_3_s7),
    .s6(conversion_affichage_4_bits_maximum_5_bits_3_s6),
    .s5(conversion_affichage_4_bits_maximum_5_bits_3_s5),
    .s4(conversion_affichage_4_bits_maximum_5_bits_3_s4),
    .s3(conversion_affichage_4_bits_maximum_5_bits_3_s3),
    .s2(conversion_affichage_4_bits_maximum_5_bits_3_s2),
    .s1(conversion_affichage_4_bits_maximum_5_bits_3_s1), .s0(conversion_affichage_4_bits_maximum_5_bits_3_s0));
  _7_segments u_7_segments_1 (
    .D(conversion_affichage_4_bits_maximum_5_bits_1_s7), .C(conversion_affichage_4_bits_maximum_5_bits_1_s6),
    .B(conversion_affichage_4_bits_maximum_5_bits_1_s5), .A(conversion_affichage_4_bits_maximum_5_bits_1_s4),
    .a_2(n7_segments_1_a_2), .f(n7_segments_1_f), .g(n7_segments_1_g), .e(n7_segments_1_e),
    .d_2(n7_segments_1_d_2), .b_2(n7_segments_1_b_2), .c_2(n7_segments_1_c_2));
  _7_Segment_Display u_7_segment_display_1 (
    .g(n7_segments_1_g), .f(n7_segments_1_f), .a(n7_segments_1_a_2), .b(n7_segments_1_b_2),
    .e(n7_segments_1_e), .d(n7_segments_1_d_2), .c(n7_segments_1_c_2));  // open: dp
  _7_segments u_7_segments_2 (
    .D(conversion_affichage_4_bits_maximum_5_bits_2_s7), .C(conversion_affichage_4_bits_maximum_5_bits_2_s6),
    .B(conversion_affichage_4_bits_maximum_5_bits_2_s5), .A(conversion_affichage_4_bits_maximum_5_bits_2_s4),
    .a_2(n7_segments_2_a_2), .f(n7_segments_2_f), .g(n7_segments_2_g), .e(n7_segments_2_e),
    .d_2(n7_segments_2_d_2), .b_2(n7_segments_2_b_2), .c_2(n7_segments_2_c_2));
  _7_Segment_Display u_7_segment_display_2 (
    .g(n7_segments_2_g), .f(n7_segments_2_f), .a(n7_segments_2_a_2), .b(n7_segments_2_b_2),
    .e(n7_segments_2_e), .d(n7_segments_2_d_2), .c(n7_segments_2_c_2));  // open: dp
  _7_segments u_7_segments_3 (
    .D(conversion_affichage_4_bits_maximum_5_bits_3_s7), .C(conversion_affichage_4_bits_maximum_5_bits_3_s6),
    .B(conversion_affichage_4_bits_maximum_5_bits_3_s5), .A(conversion_affichage_4_bits_maximum_5_bits_3_s4),
    .a_2(n7_segments_3_a_2), .f(n7_segments_3_f), .g(n7_segments_3_g), .e(n7_segments_3_e),
    .d_2(n7_segments_3_d_2), .b_2(n7_segments_3_b_2), .c_2(n7_segments_3_c_2));
  _7_Segment_Display u_7_segment_display_3 (
    .g(n7_segments_3_g), .f(n7_segments_3_f), .a(n7_segments_3_a_2), .b(n7_segments_3_b_2),
    .e(n7_segments_3_e), .d(n7_segments_3_d_2), .c(n7_segments_3_c_2));  // open: dp
  _7_Segment_Display u_7_segment_display_4 (
    .g(n7_segments_4_g), .f(n7_segments_4_f), .a(n7_segments_4_a_2), .b(n7_segments_4_b_2),
    .e(n7_segments_4_e), .d(n7_segments_4_d_2), .c(n7_segments_4_c_2));  // open: dp
  _7_segments u_7_segments_4 (
    .D(conversion_affichage_4_bits_maximum_5_bits_1_s3), .C(conversion_affichage_4_bits_maximum_5_bits_1_s2),
    .B(conversion_affichage_4_bits_maximum_5_bits_1_s1), .A(conversion_affichage_4_bits_maximum_5_bits_1_s0),
    .a_2(n7_segments_4_a_2), .f(n7_segments_4_f), .g(n7_segments_4_g), .e(n7_segments_4_e),
    .d_2(n7_segments_4_d_2), .b_2(n7_segments_4_b_2), .c_2(n7_segments_4_c_2));
  _7_Segment_Display u_7_segment_display_5 (
    .g(n7_segments_5_g), .f(n7_segments_5_f), .a(n7_segments_5_a_2), .b(n7_segments_5_b_2),
    .e(n7_segments_5_e), .d(n7_segments_5_d_2), .c(n7_segments_5_c_2));  // open: dp
  _7_segments u_7_segments_5 (
    .D(conversion_affichage_4_bits_maximum_5_bits_2_s3), .C(conversion_affichage_4_bits_maximum_5_bits_2_s2),
    .B(conversion_affichage_4_bits_maximum_5_bits_2_s1), .A(conversion_affichage_4_bits_maximum_5_bits_2_s0),
    .a_2(n7_segments_5_a_2), .f(n7_segments_5_f), .g(n7_segments_5_g), .e(n7_segments_5_e),
    .d_2(n7_segments_5_d_2), .b_2(n7_segments_5_b_2), .c_2(n7_segments_5_c_2));
  _7_Segment_Display u_7_segment_display_6 (
    .g(n7_segments_6_g), .f(n7_segments_6_f), .a(n7_segments_6_a_2), .b(n7_segments_6_b_2),
    .e(n7_segments_6_e), .d(n7_segments_6_d_2), .c(n7_segments_6_c_2));  // open: dp
  _7_segments u_7_segments_6 (
    .D(conversion_affichage_4_bits_maximum_5_bits_3_s3), .C(conversion_affichage_4_bits_maximum_5_bits_3_s2),
    .B(conversion_affichage_4_bits_maximum_5_bits_3_s1), .A(conversion_affichage_4_bits_maximum_5_bits_3_s0),
    .a_2(n7_segments_6_a_2), .f(n7_segments_6_f), .g(n7_segments_6_g), .e(n7_segments_6_e),
    .d_2(n7_segments_6_d_2), .b_2(n7_segments_6_b_2), .c_2(n7_segments_6_c_2));
endmodule

module _4_bits___4_bits (
  input  [3:0] in_1,
  input  [3:0] in_2,
  output [3:0] out_3
);

  wire conversion_affichage_4_bits_maximum_5_bits_1_s0, conversion_affichage_4_bits_maximum_5_bits_1_s1,
       conversion_affichage_4_bits_maximum_5_bits_1_s2, conversion_affichage_4_bits_maximum_5_bits_1_s3,
       conversion_affichage_4_bits_maximum_5_bits_1_s4, conversion_affichage_4_bits_maximum_5_bits_1_s5,
       conversion_affichage_4_bits_maximum_5_bits_1_s6, conversion_affichage_4_bits_maximum_5_bits_1_s7,
       conversion_affichage_4_bits_maximum_5_bits_2_s0, conversion_affichage_4_bits_maximum_5_bits_2_s1,
       conversion_affichage_4_bits_maximum_5_bits_2_s2, conversion_affichage_4_bits_maximum_5_bits_2_s3,
       conversion_affichage_4_bits_maximum_5_bits_2_s4, conversion_affichage_4_bits_maximum_5_bits_2_s5,
       conversion_affichage_4_bits_maximum_5_bits_2_s6, conversion_affichage_4_bits_maximum_5_bits_2_s7,
       conversion_affichage_4_bits_maximum_5_bits_3_s0, conversion_affichage_4_bits_maximum_5_bits_3_s1,
       conversion_affichage_4_bits_maximum_5_bits_3_s2, conversion_affichage_4_bits_maximum_5_bits_3_s3,
       conversion_affichage_4_bits_maximum_5_bits_3_s4, conversion_affichage_4_bits_maximum_5_bits_3_s5,
       conversion_affichage_4_bits_maximum_5_bits_3_s6, conversion_affichage_4_bits_maximum_5_bits_3_s7,
       n7_segments_1_a_2, n7_segments_1_b_2, n7_segments_1_c_2, n7_segments_1_d_2, n7_segments_1_e,
       n7_segments_1_f, n7_segments_1_g, n7_segments_2_a_2, n7_segments_2_b_2, n7_segments_2_c_2,
       n7_segments_2_d_2, n7_segments_2_e, n7_segments_2_f, n7_segments_2_g, n7_segments_3_a_2,
       n7_segments_3_b_2, n7_segments_3_c_2, n7_segments_3_d_2, n7_segments_3_e, n7_segments_3_f,
       n7_segments_3_g, n7_segments_4_a_2, n7_segments_4_b_2, n7_segments_4_c_2, n7_segments_4_d_2,
       n7_segments_4_e, n7_segments_4_f, n7_segments_4_g, n7_segments_5_a_2, n7_segments_5_b_2,
       n7_segments_5_c_2, n7_segments_5_d_2, n7_segments_5_e, n7_segments_5_f, n7_segments_5_g,
       n7_segments_6_a_2, n7_segments_6_b_2, n7_segments_6_c_2, n7_segments_6_d_2, n7_segments_6_e,
       n7_segments_6_f, n7_segments_6_g;

  Subtractor #(.width(4)) subtractor_1 (.a(in_1), .b(in_2), .out(out_3));  // open: bin, bout
  conversion_affichage_4_bits_maximum_5_bits conversion_affichage_4_bits_maximum_5_bits_1 (
    .e4(1'b0), .e3(in_1[3]), .e2(in_1[2]), .e1(in_1[1]), .e0(in_1[0]),
    .s7(conversion_affichage_4_bits_maximum_5_bits_1_s7),
    .s6(conversion_affichage_4_bits_maximum_5_bits_1_s6),
    .s5(conversion_affichage_4_bits_maximum_5_bits_1_s5),
    .s4(conversion_affichage_4_bits_maximum_5_bits_1_s4),
    .s3(conversion_affichage_4_bits_maximum_5_bits_1_s3),
    .s2(conversion_affichage_4_bits_maximum_5_bits_1_s2),
    .s1(conversion_affichage_4_bits_maximum_5_bits_1_s1), .s0(conversion_affichage_4_bits_maximum_5_bits_1_s0));
  conversion_affichage_4_bits_maximum_5_bits conversion_affichage_4_bits_maximum_5_bits_2 (
    .e4(1'b0), .e3(in_2[3]), .e2(in_2[2]), .e1(in_2[1]), .e0(in_2[0]),
    .s7(conversion_affichage_4_bits_maximum_5_bits_2_s7),
    .s6(conversion_affichage_4_bits_maximum_5_bits_2_s6),
    .s5(conversion_affichage_4_bits_maximum_5_bits_2_s5),
    .s4(conversion_affichage_4_bits_maximum_5_bits_2_s4),
    .s3(conversion_affichage_4_bits_maximum_5_bits_2_s3),
    .s2(conversion_affichage_4_bits_maximum_5_bits_2_s2),
    .s1(conversion_affichage_4_bits_maximum_5_bits_2_s1), .s0(conversion_affichage_4_bits_maximum_5_bits_2_s0));
  conversion_affichage_4_bits_maximum_5_bits conversion_affichage_4_bits_maximum_5_bits_3 (
    .e4(1'b0), .e3(out_3[3]), .e2(out_3[2]), .e1(out_3[1]), .e0(out_3[0]),
    .s7(conversion_affichage_4_bits_maximum_5_bits_3_s7),
    .s6(conversion_affichage_4_bits_maximum_5_bits_3_s6),
    .s5(conversion_affichage_4_bits_maximum_5_bits_3_s5),
    .s4(conversion_affichage_4_bits_maximum_5_bits_3_s4),
    .s3(conversion_affichage_4_bits_maximum_5_bits_3_s3),
    .s2(conversion_affichage_4_bits_maximum_5_bits_3_s2),
    .s1(conversion_affichage_4_bits_maximum_5_bits_3_s1), .s0(conversion_affichage_4_bits_maximum_5_bits_3_s0));
  _7_segments u_7_segments_1 (
    .D(conversion_affichage_4_bits_maximum_5_bits_1_s7), .C(conversion_affichage_4_bits_maximum_5_bits_1_s6),
    .B(conversion_affichage_4_bits_maximum_5_bits_1_s5), .A(conversion_affichage_4_bits_maximum_5_bits_1_s4),
    .a_2(n7_segments_1_a_2), .f(n7_segments_1_f), .g(n7_segments_1_g), .e(n7_segments_1_e),
    .d_2(n7_segments_1_d_2), .b_2(n7_segments_1_b_2), .c_2(n7_segments_1_c_2));
  _7_segments u_7_segments_2 (
    .D(conversion_affichage_4_bits_maximum_5_bits_2_s7), .C(conversion_affichage_4_bits_maximum_5_bits_2_s6),
    .B(conversion_affichage_4_bits_maximum_5_bits_2_s5), .A(conversion_affichage_4_bits_maximum_5_bits_2_s4),
    .a_2(n7_segments_2_a_2), .f(n7_segments_2_f), .g(n7_segments_2_g), .e(n7_segments_2_e),
    .d_2(n7_segments_2_d_2), .b_2(n7_segments_2_b_2), .c_2(n7_segments_2_c_2));
  _7_segments u_7_segments_3 (
    .D(conversion_affichage_4_bits_maximum_5_bits_3_s7), .C(conversion_affichage_4_bits_maximum_5_bits_3_s6),
    .B(conversion_affichage_4_bits_maximum_5_bits_3_s5), .A(conversion_affichage_4_bits_maximum_5_bits_3_s4),
    .a_2(n7_segments_3_a_2), .f(n7_segments_3_f), .g(n7_segments_3_g), .e(n7_segments_3_e),
    .d_2(n7_segments_3_d_2), .b_2(n7_segments_3_b_2), .c_2(n7_segments_3_c_2));
  _7_Segment_Display u_7_segment_display_1 (
    .g(n7_segments_1_g), .f(n7_segments_1_f), .a(n7_segments_1_a_2), .b(n7_segments_1_b_2),
    .e(n7_segments_1_e), .d(n7_segments_1_d_2), .c(n7_segments_1_c_2));  // open: dp
  _7_Segment_Display u_7_segment_display_2 (
    .g(n7_segments_2_g), .f(n7_segments_2_f), .a(n7_segments_2_a_2), .b(n7_segments_2_b_2),
    .e(n7_segments_2_e), .d(n7_segments_2_d_2), .c(n7_segments_2_c_2));  // open: dp
  _7_Segment_Display u_7_segment_display_3 (
    .g(n7_segments_3_g), .f(n7_segments_3_f), .a(n7_segments_3_a_2), .b(n7_segments_3_b_2),
    .e(n7_segments_3_e), .d(n7_segments_3_d_2), .c(n7_segments_3_c_2));  // open: dp
  _7_segments u_7_segments_4 (
    .D(conversion_affichage_4_bits_maximum_5_bits_1_s3), .C(conversion_affichage_4_bits_maximum_5_bits_1_s2),
    .B(conversion_affichage_4_bits_maximum_5_bits_1_s1), .A(conversion_affichage_4_bits_maximum_5_bits_1_s0),
    .a_2(n7_segments_4_a_2), .f(n7_segments_4_f), .g(n7_segments_4_g), .e(n7_segments_4_e),
    .d_2(n7_segments_4_d_2), .b_2(n7_segments_4_b_2), .c_2(n7_segments_4_c_2));
  _7_segments u_7_segments_5 (
    .D(conversion_affichage_4_bits_maximum_5_bits_2_s3), .C(conversion_affichage_4_bits_maximum_5_bits_2_s2),
    .B(conversion_affichage_4_bits_maximum_5_bits_2_s1), .A(conversion_affichage_4_bits_maximum_5_bits_2_s0),
    .a_2(n7_segments_5_a_2), .f(n7_segments_5_f), .g(n7_segments_5_g), .e(n7_segments_5_e),
    .d_2(n7_segments_5_d_2), .b_2(n7_segments_5_b_2), .c_2(n7_segments_5_c_2));
  _7_segments u_7_segments_6 (
    .D(conversion_affichage_4_bits_maximum_5_bits_3_s3), .C(conversion_affichage_4_bits_maximum_5_bits_3_s2),
    .B(conversion_affichage_4_bits_maximum_5_bits_3_s1), .A(conversion_affichage_4_bits_maximum_5_bits_3_s0),
    .a_2(n7_segments_6_a_2), .f(n7_segments_6_f), .g(n7_segments_6_g), .e(n7_segments_6_e),
    .d_2(n7_segments_6_d_2), .b_2(n7_segments_6_b_2), .c_2(n7_segments_6_c_2));
  _7_Segment_Display u_7_segment_display_4 (
    .g(n7_segments_4_g), .f(n7_segments_4_f), .a(n7_segments_4_a_2), .b(n7_segments_4_b_2),
    .e(n7_segments_4_e), .d(n7_segments_4_d_2), .c(n7_segments_4_c_2));  // open: dp
  _7_Segment_Display u_7_segment_display_5 (
    .g(n7_segments_5_g), .f(n7_segments_5_f), .a(n7_segments_5_a_2), .b(n7_segments_5_b_2),
    .e(n7_segments_5_e), .d(n7_segments_5_d_2), .c(n7_segments_5_c_2));  // open: dp
  _7_Segment_Display u_7_segment_display_6 (
    .g(n7_segments_6_g), .f(n7_segments_6_f), .a(n7_segments_6_a_2), .b(n7_segments_6_b_2),
    .e(n7_segments_6_e), .d(n7_segments_6_d_2), .c(n7_segments_6_c_2));  // open: dp
endmodule

module add3 (
  input  e0,
  input  e1,
  input  e2,
  input  e3,
  output s0,
  output s1,
  output s2,
  output s3
);

  wire and_1_out, and_2_out, and_3_out, and_4_out, and_5_out, and_6_out, and_7_out, and_8_out, and_9_out,
       not_1_out, not_2_out, not_3_out, not_4_out, not_5_out, not_6_out, not_7_out, not_8_out, not_9_out,
       not_10_out, not_11_out, not_12_out, not_13_out, not_14_out, not_15_out, not_16_out, not_17_out,
       not_18_out, not_19_out, not_20_out, not_21_out;

  and and_1 (and_1_out, not_4_out, not_1_out, not_2_out, e0);
  not not_1 (not_1_out, e2);
  not not_2 (not_2_out, e1);
  not not_3 (not_3_out, e3);
  not not_4 (not_4_out, e3);
  and and_2 (and_2_out, not_3_out, not_5_out, e1, not_8_out);
  and and_3 (and_3_out, not_7_out, not_6_out, e1, e0);
  not not_5 (not_5_out, e2);
  not not_6 (not_6_out, e2);
  not not_7 (not_7_out, e3);
  not not_8 (not_8_out, e0);
  and and_4 (and_4_out, not_12_out, e2, not_10_out, not_11_out);
  not not_9 (not_9_out, e3);
  not not_10 (not_10_out, e1);
  not not_11 (not_11_out, e0);
  not not_12 (not_12_out, e3);
  and and_5 (and_5_out, not_13_out, e2, e1, not_14_out);
  and and_6 (and_6_out, not_9_out, e2, not_15_out, e0);
  not not_13 (not_13_out, e3);
  not not_14 (not_14_out, e0);
  not not_15 (not_15_out, e1);
  and and_7 (and_7_out, not_17_out, e2, e1, e0);
  and and_8 (and_8_out, e3, not_16_out, not_21_out, not_19_out);
  not not_16 (not_16_out, e2);
  not not_17 (not_17_out, e3);
  or or_1 (s3, and_6_out, and_5_out, and_7_out, and_8_out, and_9_out);
  and and_9 (and_9_out, e3, not_20_out, not_18_out, e0);
  not not_18 (not_18_out, e1);
  not not_19 (not_19_out, e0);
  not not_20 (not_20_out, e2);
  not not_21 (not_21_out, e1);
  or or_2 (s0, and_1_out, and_3_out, and_5_out, and_8_out);
  or or_3 (s1, and_2_out, and_3_out, and_7_out, and_8_out);
  or or_4 (s2, and_4_out, and_9_out);
endmodule

module conversion_affichage_entier_de_4_chiffres_maximum_5_chiffres (
  input  [15:0] e,
  output [19:0] s
);

  wire add3_1_s0, add3_1_s1, add3_1_s2, add3_1_s3, add3_2_s0, add3_2_s1, add3_2_s2, add3_2_s3, add3_3_s0,
       add3_3_s1, add3_3_s2, add3_3_s3, add3_4_s0, add3_4_s1, add3_4_s2, add3_4_s3, add3_5_s0, add3_5_s1,
       add3_5_s2, add3_5_s3, add3_6_s0, add3_6_s1, add3_6_s2, add3_6_s3, add3_7_s0, add3_7_s1, add3_7_s2,
       add3_7_s3, add3_8_s0, add3_8_s1, add3_8_s2, add3_8_s3, add3_9_s0, add3_9_s1, add3_9_s2, add3_9_s3,
       add3_10_s0, add3_10_s1, add3_10_s2, add3_10_s3, add3_11_s0, add3_11_s1, add3_11_s2, add3_11_s3,
       add3_12_s0, add3_12_s1, add3_12_s2, add3_12_s3, add3_13_s0, add3_13_s1, add3_13_s2, add3_13_s3,
       add3_14_s0, add3_14_s1, add3_14_s2, add3_14_s3, add3_15_s0, add3_15_s1, add3_15_s2, add3_15_s3,
       add3_16_s0, add3_16_s1, add3_16_s2, add3_16_s3, add3_17_s0, add3_17_s1, add3_17_s2, add3_17_s3,
       add3_18_s0, add3_18_s1, add3_18_s2, add3_18_s3, add3_19_s0, add3_19_s1, add3_19_s2, add3_19_s3,
       add3_20_s0, add3_20_s1, add3_20_s2, add3_20_s3, add3_21_s0, add3_21_s1, add3_21_s2, add3_21_s3,
       add3_22_s0, add3_22_s1, add3_22_s2, add3_24_s0, add3_24_s1, add3_24_s2, add3_24_s3, add3_25_s0,
       add3_25_s1, add3_25_s2, add3_25_s3, add3_27_s0, add3_27_s1, add3_27_s2, add3_27_s3, add3_28_s0,
       add3_28_s1, add3_28_s2, add3_28_s3, add3_30_s0, add3_30_s1, add3_30_s2, add3_30_s3, add3_31_s0,
       add3_31_s1, add3_31_s2, add3_31_s3, add3_33_s0, add3_33_s1, add3_33_s2, add3_34_s0, add3_34_s1,
       add3_34_s2;

  add3 add3_1 (
    .e0(e[12]), .e1(add3_2_s0), .e2(add3_2_s1), .e3(add3_2_s2), .s0(add3_1_s0), .s1(add3_1_s1),
    .s2(add3_1_s2), .s3(add3_1_s3));
  add3 add3_2 (
    .e0(e[13]), .e1(e[14]), .e2(e[15]), .e3(1'b0), .s0(add3_2_s0), .s1(add3_2_s1), .s2(add3_2_s2),
    .s3(add3_2_s3));
  add3 add3_3 (
    .e0(e[9]), .e1(add3_4_s0), .e2(add3_4_s1), .e3(add3_4_s2), .s0(add3_3_s0), .s1(add3_3_s1),
    .s2(add3_3_s2), .s3(add3_3_s3));
  add3 add3_4 (
    .e0(e[10]), .e1(add3_5_s0), .e2(add3_5_s1), .e3(add3_5_s2), .s0(add3_4_s0), .s1(add3_4_s1),
    .s2(add3_4_s2), .s3(add3_4_s3));
  add3 add3_5 (
    .e0(e[11]), .e1(add3_1_s0), .e2(add3_1_s1), .e3(add3_1_s2), .s0(add3_5_s0), .s1(add3_5_s1),
    .s2(add3_5_s2), .s3(add3_5_s3));
  add3 add3_6 (
    .e0(add3_4_s3), .e1(add3_7_s0), .e2(add3_7_s1), .e3(add3_7_s2), .s0(add3_6_s0), .s1(add3_6_s1),
    .s2(add3_6_s2), .s3(add3_6_s3));
  add3 add3_7 (
    .e0(add3_5_s3), .e1(add3_1_s3), .e2(add3_2_s3), .e3(1'b0), .s0(add3_7_s0), .s1(add3_7_s1),
    .s2(add3_7_s2), .s3(add3_7_s3));
  add3 add3_8 (
    .e0(e[7]), .e1(add3_9_s0), .e2(add3_9_s1), .e3(add3_9_s2), .s0(add3_8_s0), .s1(add3_8_s1),
    .s2(add3_8_s2), .s3(add3_8_s3));
  add3 add3_9 (
    .e0(e[8]), .e1(add3_3_s0), .e2(add3_3_s1), .e3(add3_3_s2), .s0(add3_9_s0), .s1(add3_9_s1),
    .s2(add3_9_s2), .s3(add3_9_s3));
  add3 add3_10 (
    .e0(add3_9_s3), .e1(add3_11_s0), .e2(add3_11_s1), .e3(add3_11_s2), .s0(add3_10_s0), .s1(add3_10_s1),
    .s2(add3_10_s2), .s3(add3_10_s3));
  add3 add3_11 (
    .e0(add3_3_s3), .e1(add3_6_s0), .e2(add3_6_s1), .e3(add3_6_s2), .s0(add3_11_s0), .s1(add3_11_s1),
    .s2(add3_11_s2), .s3(add3_11_s3));
  add3 add3_12 (
    .e0(add3_11_s3), .e1(add3_6_s3), .e2(add3_7_s3), .e3(1'b0), .s0(add3_12_s0), .s1(add3_12_s1),
    .s2(add3_12_s2), .s3(add3_12_s3));
  add3 add3_13 (
    .e0(e[4]), .e1(add3_14_s0), .e2(add3_14_s1), .e3(add3_14_s2), .s0(add3_13_s0), .s1(add3_13_s1),
    .s2(add3_13_s2), .s3(add3_13_s3));
  add3 add3_14 (
    .e0(e[5]), .e1(add3_15_s0), .e2(add3_15_s1), .e3(add3_15_s2), .s0(add3_14_s0), .s1(add3_14_s1),
    .s2(add3_14_s2), .s3(add3_14_s3));
  add3 add3_15 (
    .e0(e[6]), .e1(add3_8_s0), .e2(add3_8_s1), .e3(add3_8_s2), .s0(add3_15_s0), .s1(add3_15_s1),
    .s2(add3_15_s2), .s3(add3_15_s3));
  add3 add3_16 (
    .e0(add3_14_s3), .e1(add3_17_s0), .e2(add3_17_s1), .e3(add3_17_s2), .s0(add3_16_s0), .s1(add3_16_s1),
    .s2(add3_16_s2), .s3(add3_16_s3));
  add3 add3_17 (
    .e0(add3_15_s3), .e1(add3_18_s0), .e2(add3_18_s1), .e3(add3_18_s2), .s0(add3_17_s0), .s1(add3_17_s1),
    .s2(add3_17_s2), .s3(add3_17_s3));
  add3 add3_18 (
    .e0(add3_8_s3), .e1(add3_10_s0), .e2(add3_10_s1), .e3(add3_10_s2), .s0(add3_18_s0), .s1(add3_18_s1),
    .s2(add3_18_s2), .s3(add3_18_s3));
  add3 add3_19 (
    .e0(add3_17_s3), .e1(add3_20_s0), .e2(add3_20_s1), .e3(add3_20_s2), .s0(add3_19_s0), .s1(add3_19_s1),
    .s2(add3_19_s2), .s3(add3_19_s3));
  add3 add3_20 (
    .e0(add3_18_s3), .e1(add3_21_s0), .e2(add3_21_s1), .e3(add3_21_s2), .s0(add3_20_s0), .s1(add3_20_s1),
    .s2(add3_20_s2), .s3(add3_20_s3));
  add3 add3_21 (
    .e0(add3_10_s3), .e1(add3_12_s0), .e2(add3_12_s1), .e3(add3_12_s2), .s0(add3_21_s0), .s1(add3_21_s1),
    .s2(add3_21_s2), .s3(add3_21_s3));
  add3 add3_22 (
    .e0(add3_20_s3), .e1(add3_21_s3), .e2(add3_12_s3), .e3(1'b0), .s0(add3_22_s0), .s1(add3_22_s1),
    .s2(add3_22_s2), .s3(s[19]));
  add3 add3_23 (
    .e0(e[1]), .e1(add3_24_s0), .e2(add3_24_s1), .e3(add3_24_s2), .s0(s[1]), .s1(s[2]), .s2(s[3]), .s3(s[4]));
  add3 add3_24 (
    .e0(e[2]), .e1(add3_25_s0), .e2(add3_25_s1), .e3(add3_25_s2), .s0(add3_24_s0), .s1(add3_24_s1),
    .s2(add3_24_s2), .s3(add3_24_s3));
  add3 add3_25 (
    .e0(e[3]), .e1(add3_13_s0), .e2(add3_13_s1), .e3(add3_13_s2), .s0(add3_25_s0), .s1(add3_25_s1),
    .s2(add3_25_s2), .s3(add3_25_s3));
  add3 add3_26 (
    .e0(add3_24_s3), .e1(add3_27_s0), .e2(add3_27_s1), .e3(add3_27_s2), .s0(s[5]), .s1(s[6]), .s2(s[7]),
    .s3(s[8]));
  add3 add3_27 (
    .e0(add3_25_s3), .e1(add3_28_s0), .e2(add3_28_s1), .e3(add3_28_s2), .s0(add3_27_s0), .s1(add3_27_s1),
    .s2(add3_27_s2), .s3(add3_27_s3));
  add3 add3_28 (
    .e0(add3_13_s3), .e1(add3_16_s0), .e2(add3_16_s1), .e3(add3_16_s2), .s0(add3_28_s0), .s1(add3_28_s1),
    .s2(add3_28_s2), .s3(add3_28_s3));
  add3 add3_29 (
    .e0(add3_27_s3), .e1(add3_30_s0), .e2(add3_30_s1), .e3(add3_30_s2), .s0(s[9]), .s1(s[10]), .s2(s[11]),
    .s3(s[12]));
  add3 add3_30 (
    .e0(add3_28_s3), .e1(add3_31_s0), .e2(add3_31_s1), .e3(add3_31_s2), .s0(add3_30_s0), .s1(add3_30_s1),
    .s2(add3_30_s2), .s3(add3_30_s3));
  add3 add3_31 (
    .e0(add3_16_s3), .e1(add3_19_s0), .e2(add3_19_s1), .e3(add3_19_s2), .s0(add3_31_s0), .s1(add3_31_s1),
    .s2(add3_31_s2), .s3(add3_31_s3));
  add3 add3_32 (
    .e0(add3_30_s3), .e1(add3_33_s0), .e2(add3_33_s1), .e3(add3_33_s2), .s0(s[13]), .s1(s[14]), .s2(s[15]),
    .s3(s[16]));
  add3 add3_33 (
    .e0(add3_31_s3), .e1(add3_34_s0), .e2(add3_34_s1), .e3(add3_34_s2), .s0(add3_33_s0), .s1(add3_33_s1),
    .s2(add3_33_s2), .s3(s[17]));
  add3 add3_34 (
    .e0(add3_19_s3), .e1(add3_22_s0), .e2(add3_22_s1), .e3(add3_22_s2), .s0(add3_34_s0), .s1(add3_34_s1),
    .s2(add3_34_s2), .s3(s[18]));

  assign s[0] = e[0];
endmodule

module \démo__4_chiffres___4_chiffres  (
  input  [15:0] e1,
  input  [15:0] e2,
  output [15:0] s
);

  wire bit_bit_et_retenue_1_retenue, bit_bit_et_retenue_2_retenue, bit_bit_et_retenue_3_retenue,
       bit_bit_et_retenue_4_retenue, bit_bit_et_retenue_5_retenue, bit_bit_et_retenue_6_retenue,
       bit_bit_et_retenue_7_retenue, bit_bit_et_retenue_8_retenue, bit_bit_et_retenue_9_retenue,
       bit_bit_et_retenue_10_retenue, bit_bit_et_retenue_11_retenue, bit_bit_et_retenue_12_retenue,
       bit_bit_et_retenue_13_retenue;

  bit___bit_et_retenue bit_bit_et_retenue_1 (
    .bit_1(e1[0]), .bit_2(e2[0]), .bit_3(1'b0), .bit_de_sortie(s[0]), .retenue(bit_bit_et_retenue_1_retenue));
  bit___bit_et_retenue bit_bit_et_retenue_2 (
    .bit_1(e1[2]), .bit_2(e2[2]), .bit_3(bit_bit_et_retenue_3_retenue), .bit_de_sortie(s[2]),
    .retenue(bit_bit_et_retenue_2_retenue));
  bit___bit_et_retenue bit_bit_et_retenue_3 (
    .bit_1(e1[1]), .bit_2(e2[1]), .bit_3(bit_bit_et_retenue_1_retenue), .bit_de_sortie(s[1]),
    .retenue(bit_bit_et_retenue_3_retenue));
  bit___bit_et_retenue bit_bit_et_retenue_4 (
    .bit_1(e1[3]), .bit_2(e2[3]), .bit_3(bit_bit_et_retenue_2_retenue), .bit_de_sortie(s[3]),
    .retenue(bit_bit_et_retenue_4_retenue));
  bit___bit_et_retenue bit_bit_et_retenue_5 (
    .bit_1(e1[4]), .bit_2(e2[4]), .bit_3(bit_bit_et_retenue_4_retenue), .bit_de_sortie(s[4]),
    .retenue(bit_bit_et_retenue_5_retenue));
  bit___bit_et_retenue bit_bit_et_retenue_6 (
    .bit_1(e1[6]), .bit_2(e2[6]), .bit_3(bit_bit_et_retenue_7_retenue), .bit_de_sortie(s[6]),
    .retenue(bit_bit_et_retenue_6_retenue));
  bit___bit_et_retenue bit_bit_et_retenue_7 (
    .bit_1(e1[5]), .bit_2(e2[5]), .bit_3(bit_bit_et_retenue_5_retenue), .bit_de_sortie(s[5]),
    .retenue(bit_bit_et_retenue_7_retenue));
  bit___bit_et_retenue bit_bit_et_retenue_8 (
    .bit_1(e1[7]), .bit_2(e2[7]), .bit_3(bit_bit_et_retenue_6_retenue), .bit_de_sortie(s[7]),
    .retenue(bit_bit_et_retenue_8_retenue));
  bit___bit_et_retenue bit_bit_et_retenue_9 (
    .bit_1(e1[8]), .bit_2(e2[8]), .bit_3(bit_bit_et_retenue_8_retenue), .bit_de_sortie(s[8]),
    .retenue(bit_bit_et_retenue_9_retenue));
  bit___bit_et_retenue bit_bit_et_retenue_10 (
    .bit_1(e1[10]), .bit_2(e2[10]), .bit_3(bit_bit_et_retenue_11_retenue), .bit_de_sortie(s[10]),
    .retenue(bit_bit_et_retenue_10_retenue));
  bit___bit_et_retenue bit_bit_et_retenue_11 (
    .bit_1(e1[9]), .bit_2(e2[9]), .bit_3(bit_bit_et_retenue_9_retenue), .bit_de_sortie(s[9]),
    .retenue(bit_bit_et_retenue_11_retenue));
  bit___bit_et_retenue bit_bit_et_retenue_12 (
    .bit_1(e1[11]), .bit_2(e2[11]), .bit_3(bit_bit_et_retenue_10_retenue), .bit_de_sortie(s[11]),
    .retenue(bit_bit_et_retenue_12_retenue));
  bit___bit_et_retenue bit_bit_et_retenue_13 (
    .bit_1(e1[12]), .bit_2(e2[12]), .bit_3(bit_bit_et_retenue_12_retenue), .bit_de_sortie(s[12]),
    .retenue(bit_bit_et_retenue_13_retenue));
  bit___bit_et_retenue bit_bit_et_retenue_14 (
    .bit_1(e1[13]), .bit_2(e2[13]), .bit_3(bit_bit_et_retenue_13_retenue), .bit_de_sortie(s[13]),
    .retenue(s[14]));

  assign s[15] = 1'b0;
  // also tied to GND on the sheet: {e1[14], e1[15], e2[14], e2[15]}
endmodule

module affichage_4_chiffres___4_chiffres (
  input  [15:0] in_1,
  input  [15:0] in_2
);

  wire n7_segments_1_a_2, n7_segments_1_b_2, n7_segments_1_c_2, n7_segments_1_d_2, n7_segments_1_e,
       n7_segments_1_f, n7_segments_1_g, n7_segments_2_a_2, n7_segments_2_b_2, n7_segments_2_c_2,
       n7_segments_2_d_2, n7_segments_2_e, n7_segments_2_f, n7_segments_2_g, n7_segments_3_a_2,
       n7_segments_3_b_2, n7_segments_3_c_2, n7_segments_3_d_2, n7_segments_3_e, n7_segments_3_f,
       n7_segments_3_g, n7_segments_4_a_2, n7_segments_4_b_2, n7_segments_4_c_2, n7_segments_4_d_2,
       n7_segments_4_e, n7_segments_4_f, n7_segments_4_g, n7_segments_5_a_2, n7_segments_5_b_2,
       n7_segments_5_c_2, n7_segments_5_d_2, n7_segments_5_e, n7_segments_5_f, n7_segments_5_g,
       n7_segments_6_a_2, n7_segments_6_b_2, n7_segments_6_c_2, n7_segments_6_d_2, n7_segments_6_e,
       n7_segments_6_f, n7_segments_6_g, n7_segments_7_a_2, n7_segments_7_b_2, n7_segments_7_c_2,
       n7_segments_7_d_2, n7_segments_7_e, n7_segments_7_f, n7_segments_7_g, n7_segments_8_a_2,
       n7_segments_8_b_2, n7_segments_8_c_2, n7_segments_8_d_2, n7_segments_8_e, n7_segments_8_f,
       n7_segments_8_g, n7_segments_9_a_2, n7_segments_9_b_2, n7_segments_9_c_2, n7_segments_9_d_2,
       n7_segments_9_e, n7_segments_9_f, n7_segments_9_g, n7_segments_10_a_2, n7_segments_10_b_2,
       n7_segments_10_c_2, n7_segments_10_d_2, n7_segments_10_e, n7_segments_10_f, n7_segments_10_g,
       n7_segments_11_a_2, n7_segments_11_b_2, n7_segments_11_c_2, n7_segments_11_d_2, n7_segments_11_e,
       n7_segments_11_f, n7_segments_11_g, n7_segments_12_a_2, n7_segments_12_b_2, n7_segments_12_c_2,
       n7_segments_12_d_2, n7_segments_12_e, n7_segments_12_f, n7_segments_12_g, n7_segments_13_a_2,
       n7_segments_13_b_2, n7_segments_13_c_2, n7_segments_13_d_2, n7_segments_13_e, n7_segments_13_f,
       n7_segments_13_g, n7_segments_14_a_2, n7_segments_14_b_2, n7_segments_14_c_2, n7_segments_14_d_2,
       n7_segments_14_e, n7_segments_14_f, n7_segments_14_g, n7_segments_15_a_2, n7_segments_15_b_2,
       n7_segments_15_c_2, n7_segments_15_d_2, n7_segments_15_e, n7_segments_15_f, n7_segments_15_g;
  wire [15:0] \démo_4_chiffres_4_chiffres_1_s ;
  wire [19:0] conversion_affichage_entier_de_4_chiffres_maximum_5_chiffres_1_s,
       conversion_affichage_entier_de_4_chiffres_maximum_5_chiffres_2_s,
       conversion_affichage_entier_de_4_chiffres_maximum_5_chiffres_3_s;

  _7_Segment_Display u_7_segment_display_1 (
    .g(n7_segments_1_g), .f(n7_segments_1_f), .a(n7_segments_1_a_2), .b(n7_segments_1_b_2),
    .e(n7_segments_1_e), .d(n7_segments_1_d_2), .c(n7_segments_1_c_2));  // open: dp
  _7_segments u_7_segments_1 (
    .D(conversion_affichage_entier_de_4_chiffres_maximum_5_chiffres_1_s[19]),
    .C(conversion_affichage_entier_de_4_chiffres_maximum_5_chiffres_1_s[18]),
    .B(conversion_affichage_entier_de_4_chiffres_maximum_5_chiffres_1_s[17]),
    .A(conversion_affichage_entier_de_4_chiffres_maximum_5_chiffres_1_s[16]), .a_2(n7_segments_1_a_2),
    .f(n7_segments_1_f), .g(n7_segments_1_g), .e(n7_segments_1_e), .d_2(n7_segments_1_d_2),
    .b_2(n7_segments_1_b_2), .c_2(n7_segments_1_c_2));
  _7_segments u_7_segments_2 (
    .D(conversion_affichage_entier_de_4_chiffres_maximum_5_chiffres_2_s[19]),
    .C(conversion_affichage_entier_de_4_chiffres_maximum_5_chiffres_2_s[18]),
    .B(conversion_affichage_entier_de_4_chiffres_maximum_5_chiffres_2_s[17]),
    .A(conversion_affichage_entier_de_4_chiffres_maximum_5_chiffres_2_s[16]), .a_2(n7_segments_2_a_2),
    .f(n7_segments_2_f), .g(n7_segments_2_g), .e(n7_segments_2_e), .d_2(n7_segments_2_d_2),
    .b_2(n7_segments_2_b_2), .c_2(n7_segments_2_c_2));
  _7_Segment_Display u_7_segment_display_2 (
    .g(n7_segments_2_g), .f(n7_segments_2_f), .a(n7_segments_2_a_2), .b(n7_segments_2_b_2),
    .e(n7_segments_2_e), .d(n7_segments_2_d_2), .c(n7_segments_2_c_2));  // open: dp
  _7_Segment_Display u_7_segment_display_3 (
    .g(n7_segments_3_g), .f(n7_segments_3_f), .a(n7_segments_3_a_2), .b(n7_segments_3_b_2),
    .e(n7_segments_3_e), .d(n7_segments_3_d_2), .c(n7_segments_3_c_2));  // open: dp
  _7_segments u_7_segments_3 (
    .D(conversion_affichage_entier_de_4_chiffres_maximum_5_chiffres_1_s[15]),
    .C(conversion_affichage_entier_de_4_chiffres_maximum_5_chiffres_1_s[14]),
    .B(conversion_affichage_entier_de_4_chiffres_maximum_5_chiffres_1_s[13]),
    .A(conversion_affichage_entier_de_4_chiffres_maximum_5_chiffres_1_s[12]), .a_2(n7_segments_3_a_2),
    .f(n7_segments_3_f), .g(n7_segments_3_g), .e(n7_segments_3_e), .d_2(n7_segments_3_d_2),
    .b_2(n7_segments_3_b_2), .c_2(n7_segments_3_c_2));
  _7_segments u_7_segments_4 (
    .D(conversion_affichage_entier_de_4_chiffres_maximum_5_chiffres_2_s[15]),
    .C(conversion_affichage_entier_de_4_chiffres_maximum_5_chiffres_2_s[14]),
    .B(conversion_affichage_entier_de_4_chiffres_maximum_5_chiffres_2_s[13]),
    .A(conversion_affichage_entier_de_4_chiffres_maximum_5_chiffres_2_s[12]), .a_2(n7_segments_4_a_2),
    .f(n7_segments_4_f), .g(n7_segments_4_g), .e(n7_segments_4_e), .d_2(n7_segments_4_d_2),
    .b_2(n7_segments_4_b_2), .c_2(n7_segments_4_c_2));
  _7_Segment_Display u_7_segment_display_4 (
    .g(n7_segments_4_g), .f(n7_segments_4_f), .a(n7_segments_4_a_2), .b(n7_segments_4_b_2),
    .e(n7_segments_4_e), .d(n7_segments_4_d_2), .c(n7_segments_4_c_2));  // open: dp
  _7_segments u_7_segments_5 (
    .D(conversion_affichage_entier_de_4_chiffres_maximum_5_chiffres_1_s[11]),
    .C(conversion_affichage_entier_de_4_chiffres_maximum_5_chiffres_1_s[10]),
    .B(conversion_affichage_entier_de_4_chiffres_maximum_5_chiffres_1_s[9]),
    .A(conversion_affichage_entier_de_4_chiffres_maximum_5_chiffres_1_s[8]), .a_2(n7_segments_5_a_2),
    .f(n7_segments_5_f), .g(n7_segments_5_g), .e(n7_segments_5_e), .d_2(n7_segments_5_d_2),
    .b_2(n7_segments_5_b_2), .c_2(n7_segments_5_c_2));
  _7_Segment_Display u_7_segment_display_5 (
    .g(n7_segments_5_g), .f(n7_segments_5_f), .a(n7_segments_5_a_2), .b(n7_segments_5_b_2),
    .e(n7_segments_5_e), .d(n7_segments_5_d_2), .c(n7_segments_5_c_2));  // open: dp
  _7_Segment_Display u_7_segment_display_6 (
    .g(n7_segments_6_g), .f(n7_segments_6_f), .a(n7_segments_6_a_2), .b(n7_segments_6_b_2),
    .e(n7_segments_6_e), .d(n7_segments_6_d_2), .c(n7_segments_6_c_2));  // open: dp
  _7_segments u_7_segments_6 (
    .D(conversion_affichage_entier_de_4_chiffres_maximum_5_chiffres_2_s[11]),
    .C(conversion_affichage_entier_de_4_chiffres_maximum_5_chiffres_2_s[10]),
    .B(conversion_affichage_entier_de_4_chiffres_maximum_5_chiffres_2_s[9]),
    .A(conversion_affichage_entier_de_4_chiffres_maximum_5_chiffres_2_s[8]), .a_2(n7_segments_6_a_2),
    .f(n7_segments_6_f), .g(n7_segments_6_g), .e(n7_segments_6_e), .d_2(n7_segments_6_d_2),
    .b_2(n7_segments_6_b_2), .c_2(n7_segments_6_c_2));
  conversion_affichage_entier_de_4_chiffres_maximum_5_chiffres conversion_affichage_entier_de_4_chiffres_maximum_5_chiffres_1 (
    .e(in_1), .s(conversion_affichage_entier_de_4_chiffres_maximum_5_chiffres_1_s));
  conversion_affichage_entier_de_4_chiffres_maximum_5_chiffres conversion_affichage_entier_de_4_chiffres_maximum_5_chiffres_2 (
    .e(in_2), .s(conversion_affichage_entier_de_4_chiffres_maximum_5_chiffres_2_s));
  _7_segments u_7_segments_7 (
    .D(conversion_affichage_entier_de_4_chiffres_maximum_5_chiffres_1_s[7]),
    .C(conversion_affichage_entier_de_4_chiffres_maximum_5_chiffres_1_s[6]),
    .B(conversion_affichage_entier_de_4_chiffres_maximum_5_chiffres_1_s[5]),
    .A(conversion_affichage_entier_de_4_chiffres_maximum_5_chiffres_1_s[4]), .a_2(n7_segments_7_a_2),
    .f(n7_segments_7_f), .g(n7_segments_7_g), .e(n7_segments_7_e), .d_2(n7_segments_7_d_2),
    .b_2(n7_segments_7_b_2), .c_2(n7_segments_7_c_2));
  _7_Segment_Display u_7_segment_display_7 (
    .g(n7_segments_7_g), .f(n7_segments_7_f), .a(n7_segments_7_a_2), .b(n7_segments_7_b_2),
    .e(n7_segments_7_e), .d(n7_segments_7_d_2), .c(n7_segments_7_c_2));  // open: dp
  _7_Segment_Display u_7_segment_display_8 (
    .g(n7_segments_8_g), .f(n7_segments_8_f), .a(n7_segments_8_a_2), .b(n7_segments_8_b_2),
    .e(n7_segments_8_e), .d(n7_segments_8_d_2), .c(n7_segments_8_c_2));  // open: dp
  _7_segments u_7_segments_8 (
    .D(conversion_affichage_entier_de_4_chiffres_maximum_5_chiffres_2_s[7]),
    .C(conversion_affichage_entier_de_4_chiffres_maximum_5_chiffres_2_s[6]),
    .B(conversion_affichage_entier_de_4_chiffres_maximum_5_chiffres_2_s[5]),
    .A(conversion_affichage_entier_de_4_chiffres_maximum_5_chiffres_2_s[4]), .a_2(n7_segments_8_a_2),
    .f(n7_segments_8_f), .g(n7_segments_8_g), .e(n7_segments_8_e), .d_2(n7_segments_8_d_2),
    .b_2(n7_segments_8_b_2), .c_2(n7_segments_8_c_2));
  _7_segments u_7_segments_9 (
    .D(conversion_affichage_entier_de_4_chiffres_maximum_5_chiffres_1_s[3]),
    .C(conversion_affichage_entier_de_4_chiffres_maximum_5_chiffres_1_s[2]),
    .B(conversion_affichage_entier_de_4_chiffres_maximum_5_chiffres_1_s[1]),
    .A(conversion_affichage_entier_de_4_chiffres_maximum_5_chiffres_1_s[0]), .a_2(n7_segments_9_a_2),
    .f(n7_segments_9_f), .g(n7_segments_9_g), .e(n7_segments_9_e), .d_2(n7_segments_9_d_2),
    .b_2(n7_segments_9_b_2), .c_2(n7_segments_9_c_2));
  _7_Segment_Display u_7_segment_display_9 (
    .g(n7_segments_9_g), .f(n7_segments_9_f), .a(n7_segments_9_a_2), .b(n7_segments_9_b_2),
    .e(n7_segments_9_e), .d(n7_segments_9_d_2), .c(n7_segments_9_c_2));  // open: dp
  _7_segments u_7_segments_10 (
    .D(conversion_affichage_entier_de_4_chiffres_maximum_5_chiffres_3_s[19]),
    .C(conversion_affichage_entier_de_4_chiffres_maximum_5_chiffres_3_s[18]),
    .B(conversion_affichage_entier_de_4_chiffres_maximum_5_chiffres_3_s[17]),
    .A(conversion_affichage_entier_de_4_chiffres_maximum_5_chiffres_3_s[16]), .a_2(n7_segments_10_a_2),
    .f(n7_segments_10_f), .g(n7_segments_10_g), .e(n7_segments_10_e), .d_2(n7_segments_10_d_2),
    .b_2(n7_segments_10_b_2), .c_2(n7_segments_10_c_2));
  _7_segments u_7_segments_11 (
    .D(conversion_affichage_entier_de_4_chiffres_maximum_5_chiffres_2_s[3]),
    .C(conversion_affichage_entier_de_4_chiffres_maximum_5_chiffres_2_s[2]),
    .B(conversion_affichage_entier_de_4_chiffres_maximum_5_chiffres_2_s[1]),
    .A(conversion_affichage_entier_de_4_chiffres_maximum_5_chiffres_2_s[0]), .a_2(n7_segments_11_a_2),
    .f(n7_segments_11_f), .g(n7_segments_11_g), .e(n7_segments_11_e), .d_2(n7_segments_11_d_2),
    .b_2(n7_segments_11_b_2), .c_2(n7_segments_11_c_2));
  _7_Segment_Display u_7_segment_display_10 (
    .g(n7_segments_11_g), .f(n7_segments_11_f), .a(n7_segments_11_a_2), .b(n7_segments_11_b_2),
    .e(n7_segments_11_e), .d(n7_segments_11_d_2), .c(n7_segments_11_c_2));  // open: dp
  _7_Segment_Display u_7_segment_display_11 (
    .g(n7_segments_10_g), .f(n7_segments_10_f), .a(n7_segments_10_a_2), .b(n7_segments_10_b_2),
    .e(n7_segments_10_e), .d(n7_segments_10_d_2), .c(n7_segments_10_c_2));  // open: dp
  _7_segments u_7_segments_12 (
    .D(conversion_affichage_entier_de_4_chiffres_maximum_5_chiffres_3_s[15]),
    .C(conversion_affichage_entier_de_4_chiffres_maximum_5_chiffres_3_s[14]),
    .B(conversion_affichage_entier_de_4_chiffres_maximum_5_chiffres_3_s[13]),
    .A(conversion_affichage_entier_de_4_chiffres_maximum_5_chiffres_3_s[12]), .a_2(n7_segments_12_a_2),
    .f(n7_segments_12_f), .g(n7_segments_12_g), .e(n7_segments_12_e), .d_2(n7_segments_12_d_2),
    .b_2(n7_segments_12_b_2), .c_2(n7_segments_12_c_2));
  \démo__4_chiffres___4_chiffres  \démo_4_chiffres_4_chiffres_1  (
    .e1(in_1), .e2(in_2), .s(\démo_4_chiffres_4_chiffres_1_s ));
  _7_Segment_Display u_7_segment_display_12 (
    .g(n7_segments_12_g), .f(n7_segments_12_f), .a(n7_segments_12_a_2), .b(n7_segments_12_b_2),
    .e(n7_segments_12_e), .d(n7_segments_12_d_2), .c(n7_segments_12_c_2));  // open: dp
  _7_segments u_7_segments_13 (
    .D(conversion_affichage_entier_de_4_chiffres_maximum_5_chiffres_3_s[11]),
    .C(conversion_affichage_entier_de_4_chiffres_maximum_5_chiffres_3_s[10]),
    .B(conversion_affichage_entier_de_4_chiffres_maximum_5_chiffres_3_s[9]),
    .A(conversion_affichage_entier_de_4_chiffres_maximum_5_chiffres_3_s[8]), .a_2(n7_segments_13_a_2),
    .f(n7_segments_13_f), .g(n7_segments_13_g), .e(n7_segments_13_e), .d_2(n7_segments_13_d_2),
    .b_2(n7_segments_13_b_2), .c_2(n7_segments_13_c_2));
  _7_Segment_Display u_7_segment_display_13 (
    .g(n7_segments_13_g), .f(n7_segments_13_f), .a(n7_segments_13_a_2), .b(n7_segments_13_b_2),
    .e(n7_segments_13_e), .d(n7_segments_13_d_2), .c(n7_segments_13_c_2));  // open: dp
  conversion_affichage_entier_de_4_chiffres_maximum_5_chiffres conversion_affichage_entier_de_4_chiffres_maximum_5_chiffres_3 (
    .e(\démo_4_chiffres_4_chiffres_1_s ), .s(conversion_affichage_entier_de_4_chiffres_maximum_5_chiffres_3_s));
  _7_segments u_7_segments_14 (
    .D(conversion_affichage_entier_de_4_chiffres_maximum_5_chiffres_3_s[7]),
    .C(conversion_affichage_entier_de_4_chiffres_maximum_5_chiffres_3_s[6]),
    .B(conversion_affichage_entier_de_4_chiffres_maximum_5_chiffres_3_s[5]),
    .A(conversion_affichage_entier_de_4_chiffres_maximum_5_chiffres_3_s[4]), .a_2(n7_segments_14_a_2),
    .f(n7_segments_14_f), .g(n7_segments_14_g), .e(n7_segments_14_e), .d_2(n7_segments_14_d_2),
    .b_2(n7_segments_14_b_2), .c_2(n7_segments_14_c_2));
  _7_Segment_Display u_7_segment_display_14 (
    .g(n7_segments_14_g), .f(n7_segments_14_f), .a(n7_segments_14_a_2), .b(n7_segments_14_b_2),
    .e(n7_segments_14_e), .d(n7_segments_14_d_2), .c(n7_segments_14_c_2));  // open: dp
  _7_segments u_7_segments_15 (
    .D(conversion_affichage_entier_de_4_chiffres_maximum_5_chiffres_3_s[3]),
    .C(conversion_affichage_entier_de_4_chiffres_maximum_5_chiffres_3_s[2]),
    .B(conversion_affichage_entier_de_4_chiffres_maximum_5_chiffres_3_s[1]),
    .A(conversion_affichage_entier_de_4_chiffres_maximum_5_chiffres_3_s[0]), .a_2(n7_segments_15_a_2),
    .f(n7_segments_15_f), .g(n7_segments_15_g), .e(n7_segments_15_e), .d_2(n7_segments_15_d_2),
    .b_2(n7_segments_15_b_2), .c_2(n7_segments_15_c_2));
  _7_Segment_Display u_7_segment_display_15 (
    .g(n7_segments_15_g), .f(n7_segments_15_f), .a(n7_segments_15_a_2), .b(n7_segments_15_b_2),
    .e(n7_segments_15_e), .d(n7_segments_15_d_2), .c(n7_segments_15_c_2));  // open: dp
endmodule

module affichage_4_chiffres___4_chiffres_2 (
  input  [15:0] in_1,
  input  [15:0] in_2,
  output [15:0] out_3
);

  wire n7_segments_1_a_2, n7_segments_1_b_2, n7_segments_1_c_2, n7_segments_1_d_2, n7_segments_1_e,
       n7_segments_1_f, n7_segments_1_g, n7_segments_2_a_2, n7_segments_2_b_2, n7_segments_2_c_2,
       n7_segments_2_d_2, n7_segments_2_e, n7_segments_2_f, n7_segments_2_g, n7_segments_3_a_2,
       n7_segments_3_b_2, n7_segments_3_c_2, n7_segments_3_d_2, n7_segments_3_e, n7_segments_3_f,
       n7_segments_3_g, n7_segments_4_a_2, n7_segments_4_b_2, n7_segments_4_c_2, n7_segments_4_d_2,
       n7_segments_4_e, n7_segments_4_f, n7_segments_4_g, n7_segments_5_a_2, n7_segments_5_b_2,
       n7_segments_5_c_2, n7_segments_5_d_2, n7_segments_5_e, n7_segments_5_f, n7_segments_5_g,
       n7_segments_6_a_2, n7_segments_6_b_2, n7_segments_6_c_2, n7_segments_6_d_2, n7_segments_6_e,
       n7_segments_6_f, n7_segments_6_g, n7_segments_7_a_2, n7_segments_7_b_2, n7_segments_7_c_2,
       n7_segments_7_d_2, n7_segments_7_e, n7_segments_7_f, n7_segments_7_g, n7_segments_8_a_2,
       n7_segments_8_b_2, n7_segments_8_c_2, n7_segments_8_d_2, n7_segments_8_e, n7_segments_8_f,
       n7_segments_8_g, n7_segments_9_a_2, n7_segments_9_b_2, n7_segments_9_c_2, n7_segments_9_d_2,
       n7_segments_9_e, n7_segments_9_f, n7_segments_9_g, n7_segments_10_a_2, n7_segments_10_b_2,
       n7_segments_10_c_2, n7_segments_10_d_2, n7_segments_10_e, n7_segments_10_f, n7_segments_10_g,
       n7_segments_11_a_2, n7_segments_11_b_2, n7_segments_11_c_2, n7_segments_11_d_2, n7_segments_11_e,
       n7_segments_11_f, n7_segments_11_g, n7_segments_12_a_2, n7_segments_12_b_2, n7_segments_12_c_2,
       n7_segments_12_d_2, n7_segments_12_e, n7_segments_12_f, n7_segments_12_g, n7_segments_13_a_2,
       n7_segments_13_b_2, n7_segments_13_c_2, n7_segments_13_d_2, n7_segments_13_e, n7_segments_13_f,
       n7_segments_13_g, n7_segments_14_a_2, n7_segments_14_b_2, n7_segments_14_c_2, n7_segments_14_d_2,
       n7_segments_14_e, n7_segments_14_f, n7_segments_14_g, n7_segments_15_a_2, n7_segments_15_b_2,
       n7_segments_15_c_2, n7_segments_15_d_2, n7_segments_15_e, n7_segments_15_f, n7_segments_15_g;
  wire [19:0] conversion_affichage_entier_de_4_chiffres_maximum_5_chiffres_1_s,
       conversion_affichage_entier_de_4_chiffres_maximum_5_chiffres_2_s,
       conversion_affichage_entier_de_4_chiffres_maximum_5_chiffres_3_s;

  _7_segments u_7_segments_1 (
    .D(conversion_affichage_entier_de_4_chiffres_maximum_5_chiffres_1_s[19]),
    .C(conversion_affichage_entier_de_4_chiffres_maximum_5_chiffres_1_s[18]),
    .B(conversion_affichage_entier_de_4_chiffres_maximum_5_chiffres_1_s[17]),
    .A(conversion_affichage_entier_de_4_chiffres_maximum_5_chiffres_1_s[16]), .a_2(n7_segments_1_a_2),
    .f(n7_segments_1_f), .g(n7_segments_1_g), .e(n7_segments_1_e), .d_2(n7_segments_1_d_2),
    .b_2(n7_segments_1_b_2), .c_2(n7_segments_1_c_2));
  _7_segments u_7_segments_2 (
    .D(conversion_affichage_entier_de_4_chiffres_maximum_5_chiffres_2_s[19]),
    .C(conversion_affichage_entier_de_4_chiffres_maximum_5_chiffres_2_s[18]),
    .B(conversion_affichage_entier_de_4_chiffres_maximum_5_chiffres_2_s[17]),
    .A(conversion_affichage_entier_de_4_chiffres_maximum_5_chiffres_2_s[16]), .a_2(n7_segments_2_a_2),
    .f(n7_segments_2_f), .g(n7_segments_2_g), .e(n7_segments_2_e), .d_2(n7_segments_2_d_2),
    .b_2(n7_segments_2_b_2), .c_2(n7_segments_2_c_2));
  _7_Segment_Display u_7_segment_display_1 (
    .g(n7_segments_1_g), .f(n7_segments_1_f), .a(n7_segments_1_a_2), .b(n7_segments_1_b_2),
    .e(n7_segments_1_e), .d(n7_segments_1_d_2), .c(n7_segments_1_c_2));  // open: dp
  _7_Segment_Display u_7_segment_display_2 (
    .g(n7_segments_2_g), .f(n7_segments_2_f), .a(n7_segments_2_a_2), .b(n7_segments_2_b_2),
    .e(n7_segments_2_e), .d(n7_segments_2_d_2), .c(n7_segments_2_c_2));  // open: dp
  _7_segments u_7_segments_3 (
    .D(conversion_affichage_entier_de_4_chiffres_maximum_5_chiffres_1_s[15]),
    .C(conversion_affichage_entier_de_4_chiffres_maximum_5_chiffres_1_s[14]),
    .B(conversion_affichage_entier_de_4_chiffres_maximum_5_chiffres_1_s[13]),
    .A(conversion_affichage_entier_de_4_chiffres_maximum_5_chiffres_1_s[12]), .a_2(n7_segments_3_a_2),
    .f(n7_segments_3_f), .g(n7_segments_3_g), .e(n7_segments_3_e), .d_2(n7_segments_3_d_2),
    .b_2(n7_segments_3_b_2), .c_2(n7_segments_3_c_2));
  _7_segments u_7_segments_4 (
    .D(conversion_affichage_entier_de_4_chiffres_maximum_5_chiffres_2_s[15]),
    .C(conversion_affichage_entier_de_4_chiffres_maximum_5_chiffres_2_s[14]),
    .B(conversion_affichage_entier_de_4_chiffres_maximum_5_chiffres_2_s[13]),
    .A(conversion_affichage_entier_de_4_chiffres_maximum_5_chiffres_2_s[12]), .a_2(n7_segments_4_a_2),
    .f(n7_segments_4_f), .g(n7_segments_4_g), .e(n7_segments_4_e), .d_2(n7_segments_4_d_2),
    .b_2(n7_segments_4_b_2), .c_2(n7_segments_4_c_2));
  _7_Segment_Display u_7_segment_display_3 (
    .g(n7_segments_3_g), .f(n7_segments_3_f), .a(n7_segments_3_a_2), .b(n7_segments_3_b_2),
    .e(n7_segments_3_e), .d(n7_segments_3_d_2), .c(n7_segments_3_c_2));  // open: dp
  _7_Segment_Display u_7_segment_display_4 (
    .g(n7_segments_4_g), .f(n7_segments_4_f), .a(n7_segments_4_a_2), .b(n7_segments_4_b_2),
    .e(n7_segments_4_e), .d(n7_segments_4_d_2), .c(n7_segments_4_c_2));  // open: dp
  _7_segments u_7_segments_5 (
    .D(conversion_affichage_entier_de_4_chiffres_maximum_5_chiffres_1_s[11]),
    .C(conversion_affichage_entier_de_4_chiffres_maximum_5_chiffres_1_s[10]),
    .B(conversion_affichage_entier_de_4_chiffres_maximum_5_chiffres_1_s[9]),
    .A(conversion_affichage_entier_de_4_chiffres_maximum_5_chiffres_1_s[8]), .a_2(n7_segments_5_a_2),
    .f(n7_segments_5_f), .g(n7_segments_5_g), .e(n7_segments_5_e), .d_2(n7_segments_5_d_2),
    .b_2(n7_segments_5_b_2), .c_2(n7_segments_5_c_2));
  _7_segments u_7_segments_6 (
    .D(conversion_affichage_entier_de_4_chiffres_maximum_5_chiffres_2_s[11]),
    .C(conversion_affichage_entier_de_4_chiffres_maximum_5_chiffres_2_s[10]),
    .B(conversion_affichage_entier_de_4_chiffres_maximum_5_chiffres_2_s[9]),
    .A(conversion_affichage_entier_de_4_chiffres_maximum_5_chiffres_2_s[8]), .a_2(n7_segments_6_a_2),
    .f(n7_segments_6_f), .g(n7_segments_6_g), .e(n7_segments_6_e), .d_2(n7_segments_6_d_2),
    .b_2(n7_segments_6_b_2), .c_2(n7_segments_6_c_2));
  _7_Segment_Display u_7_segment_display_5 (
    .g(n7_segments_5_g), .f(n7_segments_5_f), .a(n7_segments_5_a_2), .b(n7_segments_5_b_2),
    .e(n7_segments_5_e), .d(n7_segments_5_d_2), .c(n7_segments_5_c_2));  // open: dp
  conversion_affichage_entier_de_4_chiffres_maximum_5_chiffres conversion_affichage_entier_de_4_chiffres_maximum_5_chiffres_1 (
    .e(in_1), .s(conversion_affichage_entier_de_4_chiffres_maximum_5_chiffres_1_s));
  _7_Segment_Display u_7_segment_display_6 (
    .g(n7_segments_6_g), .f(n7_segments_6_f), .a(n7_segments_6_a_2), .b(n7_segments_6_b_2),
    .e(n7_segments_6_e), .d(n7_segments_6_d_2), .c(n7_segments_6_c_2));  // open: dp
  conversion_affichage_entier_de_4_chiffres_maximum_5_chiffres conversion_affichage_entier_de_4_chiffres_maximum_5_chiffres_2 (
    .e(in_2), .s(conversion_affichage_entier_de_4_chiffres_maximum_5_chiffres_2_s));
  _7_segments u_7_segments_7 (
    .D(conversion_affichage_entier_de_4_chiffres_maximum_5_chiffres_1_s[7]),
    .C(conversion_affichage_entier_de_4_chiffres_maximum_5_chiffres_1_s[6]),
    .B(conversion_affichage_entier_de_4_chiffres_maximum_5_chiffres_1_s[5]),
    .A(conversion_affichage_entier_de_4_chiffres_maximum_5_chiffres_1_s[4]), .a_2(n7_segments_7_a_2),
    .f(n7_segments_7_f), .g(n7_segments_7_g), .e(n7_segments_7_e), .d_2(n7_segments_7_d_2),
    .b_2(n7_segments_7_b_2), .c_2(n7_segments_7_c_2));
  _7_segments u_7_segments_8 (
    .D(conversion_affichage_entier_de_4_chiffres_maximum_5_chiffres_2_s[7]),
    .C(conversion_affichage_entier_de_4_chiffres_maximum_5_chiffres_2_s[6]),
    .B(conversion_affichage_entier_de_4_chiffres_maximum_5_chiffres_2_s[5]),
    .A(conversion_affichage_entier_de_4_chiffres_maximum_5_chiffres_2_s[4]), .a_2(n7_segments_8_a_2),
    .f(n7_segments_8_f), .g(n7_segments_8_g), .e(n7_segments_8_e), .d_2(n7_segments_8_d_2),
    .b_2(n7_segments_8_b_2), .c_2(n7_segments_8_c_2));
  _7_Segment_Display u_7_segment_display_7 (
    .g(n7_segments_7_g), .f(n7_segments_7_f), .a(n7_segments_7_a_2), .b(n7_segments_7_b_2),
    .e(n7_segments_7_e), .d(n7_segments_7_d_2), .c(n7_segments_7_c_2));  // open: dp
  _7_Segment_Display u_7_segment_display_8 (
    .g(n7_segments_8_g), .f(n7_segments_8_f), .a(n7_segments_8_a_2), .b(n7_segments_8_b_2),
    .e(n7_segments_8_e), .d(n7_segments_8_d_2), .c(n7_segments_8_c_2));  // open: dp
  _7_segments u_7_segments_9 (
    .D(conversion_affichage_entier_de_4_chiffres_maximum_5_chiffres_1_s[3]),
    .C(conversion_affichage_entier_de_4_chiffres_maximum_5_chiffres_1_s[2]),
    .B(conversion_affichage_entier_de_4_chiffres_maximum_5_chiffres_1_s[1]),
    .A(conversion_affichage_entier_de_4_chiffres_maximum_5_chiffres_1_s[0]), .a_2(n7_segments_9_a_2),
    .f(n7_segments_9_f), .g(n7_segments_9_g), .e(n7_segments_9_e), .d_2(n7_segments_9_d_2),
    .b_2(n7_segments_9_b_2), .c_2(n7_segments_9_c_2));
  _7_segments u_7_segments_10 (
    .D(conversion_affichage_entier_de_4_chiffres_maximum_5_chiffres_2_s[3]),
    .C(conversion_affichage_entier_de_4_chiffres_maximum_5_chiffres_2_s[2]),
    .B(conversion_affichage_entier_de_4_chiffres_maximum_5_chiffres_2_s[1]),
    .A(conversion_affichage_entier_de_4_chiffres_maximum_5_chiffres_2_s[0]), .a_2(n7_segments_10_a_2),
    .f(n7_segments_10_f), .g(n7_segments_10_g), .e(n7_segments_10_e), .d_2(n7_segments_10_d_2),
    .b_2(n7_segments_10_b_2), .c_2(n7_segments_10_c_2));
  _7_Segment_Display u_7_segment_display_9 (
    .g(n7_segments_9_g), .f(n7_segments_9_f), .a(n7_segments_9_a_2), .b(n7_segments_9_b_2),
    .e(n7_segments_9_e), .d(n7_segments_9_d_2), .c(n7_segments_9_c_2));  // open: dp
  _7_Segment_Display u_7_segment_display_10 (
    .g(n7_segments_11_g), .f(n7_segments_11_f), .a(n7_segments_11_a_2), .b(n7_segments_11_b_2),
    .e(n7_segments_11_e), .d(n7_segments_11_d_2), .c(n7_segments_11_c_2));  // open: dp
  _7_segments u_7_segments_11 (
    .D(conversion_affichage_entier_de_4_chiffres_maximum_5_chiffres_3_s[19]),
    .C(conversion_affichage_entier_de_4_chiffres_maximum_5_chiffres_3_s[18]),
    .B(conversion_affichage_entier_de_4_chiffres_maximum_5_chiffres_3_s[17]),
    .A(conversion_affichage_entier_de_4_chiffres_maximum_5_chiffres_3_s[16]), .a_2(n7_segments_11_a_2),
    .f(n7_segments_11_f), .g(n7_segments_11_g), .e(n7_segments_11_e), .d_2(n7_segments_11_d_2),
    .b_2(n7_segments_11_b_2), .c_2(n7_segments_11_c_2));
  _7_Segment_Display u_7_segment_display_11 (
    .g(n7_segments_10_g), .f(n7_segments_10_f), .a(n7_segments_10_a_2), .b(n7_segments_10_b_2),
    .e(n7_segments_10_e), .d(n7_segments_10_d_2), .c(n7_segments_10_c_2));  // open: dp
  Subtractor #(.width(16)) subtractor_1 (.a(in_1), .b(in_2), .out(out_3));  // open: bin, bout
  _7_segments u_7_segments_12 (
    .D(conversion_affichage_entier_de_4_chiffres_maximum_5_chiffres_3_s[15]),
    .C(conversion_affichage_entier_de_4_chiffres_maximum_5_chiffres_3_s[14]),
    .B(conversion_affichage_entier_de_4_chiffres_maximum_5_chiffres_3_s[13]),
    .A(conversion_affichage_entier_de_4_chiffres_maximum_5_chiffres_3_s[12]), .a_2(n7_segments_12_a_2),
    .f(n7_segments_12_f), .g(n7_segments_12_g), .e(n7_segments_12_e), .d_2(n7_segments_12_d_2),
    .b_2(n7_segments_12_b_2), .c_2(n7_segments_12_c_2));
  _7_Segment_Display u_7_segment_display_12 (
    .g(n7_segments_12_g), .f(n7_segments_12_f), .a(n7_segments_12_a_2), .b(n7_segments_12_b_2),
    .e(n7_segments_12_e), .d(n7_segments_12_d_2), .c(n7_segments_12_c_2));  // open: dp
  _7_Segment_Display u_7_segment_display_13 (
    .g(n7_segments_13_g), .f(n7_segments_13_f), .a(n7_segments_13_a_2), .b(n7_segments_13_b_2),
    .e(n7_segments_13_e), .d(n7_segments_13_d_2), .c(n7_segments_13_c_2));  // open: dp
  _7_segments u_7_segments_13 (
    .D(conversion_affichage_entier_de_4_chiffres_maximum_5_chiffres_3_s[11]),
    .C(conversion_affichage_entier_de_4_chiffres_maximum_5_chiffres_3_s[10]),
    .B(conversion_affichage_entier_de_4_chiffres_maximum_5_chiffres_3_s[9]),
    .A(conversion_affichage_entier_de_4_chiffres_maximum_5_chiffres_3_s[8]), .a_2(n7_segments_13_a_2),
    .f(n7_segments_13_f), .g(n7_segments_13_g), .e(n7_segments_13_e), .d_2(n7_segments_13_d_2),
    .b_2(n7_segments_13_b_2), .c_2(n7_segments_13_c_2));
  conversion_affichage_entier_de_4_chiffres_maximum_5_chiffres conversion_affichage_entier_de_4_chiffres_maximum_5_chiffres_3 (
    .e(out_3), .s(conversion_affichage_entier_de_4_chiffres_maximum_5_chiffres_3_s));
  _7_Segment_Display u_7_segment_display_14 (
    .g(n7_segments_14_g), .f(n7_segments_14_f), .a(n7_segments_14_a_2), .b(n7_segments_14_b_2),
    .e(n7_segments_14_e), .d(n7_segments_14_d_2), .c(n7_segments_14_c_2));  // open: dp
  _7_segments u_7_segments_14 (
    .D(conversion_affichage_entier_de_4_chiffres_maximum_5_chiffres_3_s[7]),
    .C(conversion_affichage_entier_de_4_chiffres_maximum_5_chiffres_3_s[6]),
    .B(conversion_affichage_entier_de_4_chiffres_maximum_5_chiffres_3_s[5]),
    .A(conversion_affichage_entier_de_4_chiffres_maximum_5_chiffres_3_s[4]), .a_2(n7_segments_14_a_2),
    .f(n7_segments_14_f), .g(n7_segments_14_g), .e(n7_segments_14_e), .d_2(n7_segments_14_d_2),
    .b_2(n7_segments_14_b_2), .c_2(n7_segments_14_c_2));
  _7_Segment_Display u_7_segment_display_15 (
    .g(n7_segments_15_g), .f(n7_segments_15_f), .a(n7_segments_15_a_2), .b(n7_segments_15_b_2),
    .e(n7_segments_15_e), .d(n7_segments_15_d_2), .c(n7_segments_15_c_2));  // open: dp
  _7_segments u_7_segments_15 (
    .D(conversion_affichage_entier_de_4_chiffres_maximum_5_chiffres_3_s[3]),
    .C(conversion_affichage_entier_de_4_chiffres_maximum_5_chiffres_3_s[2]),
    .B(conversion_affichage_entier_de_4_chiffres_maximum_5_chiffres_3_s[1]),
    .A(conversion_affichage_entier_de_4_chiffres_maximum_5_chiffres_3_s[0]), .a_2(n7_segments_15_a_2),
    .f(n7_segments_15_f), .g(n7_segments_15_g), .e(n7_segments_15_e), .d_2(n7_segments_15_d_2),
    .b_2(n7_segments_15_b_2), .c_2(n7_segments_15_c_2));
endmodule
